// Digital circuit CC.dig as structural Verilog
module CC (
  input  CLK,
  input  btn,
  output pc,
  output MAR_operacoes,
  output MAR_operando,
  output IR
);

  wire Q1, Q3;

  ringcounter_5bits ringcounter_5bits_1 (
    .clk(CLK), .btn(btn), .Q0(MAR_operacoes), .Q1(Q1), .Q2(MAR_operando), .Q3(Q3), .Q4(pc));
  xor xor_1 (IR, Q1, Q3);

  // Other names for the same wires on the sheet: Q0 = MAR_operacoes; Q2 = MAR_operando; Q4 = pc
endmodule
