// Digital circuit CPU.dig as structural Verilog
module CPU (
  input  CLK,
  output [7:0] AC,
  output Negativo,
  output Overflow,
  output [7:0] MQ,
  output [7:0] N,
  output [2:0] Op_CODE,
  output [7:0] out_8,
  output [7:0] out_9
);

  wire button_1_out, IR, MAR_operacao, MAR_operando, pc, PC_ovf;
  wire [2:0] driver_3_out;
  wire [7:0] AC_t, IR_q, MAR_operador_q, MAR_operando_q, MQ_t;

  Register #(.Bits(8)) u_MAR_operando (.D(out_8), .C(CLK), .en(1'b1), .Q(MAR_operando_q));
  EEPROMDualPort #(.AddrBits(8), .Bits(8)) Operandos (
    .A(out_8), .Din({8{1'b0}}), .str(1'b0), .C(CLK), .ld(1'b1), .D(N));
  EEPROMDualPort #(.AddrBits(8), .Bits(3)) \Operações  (
    .A(out_8), .Din(3'b000), .str(1'b0), .C(CLK), .ld(1'b1), .D(Op_CODE));
  assign out_8 = MAR_operando ? MAR_operando_q : 8'bz;  // Driver driver_1
  Register #(.Bits(8)) MAR_operador (.D(out_8), .C(CLK), .en(1'b1), .Q(MAR_operador_q));
  CC cc_1 (.CLK(CLK), .btn(button_1_out), .pc(pc), .MAR_operacoes(MAR_operacao), .MAR_operando(MAR_operando), .IR(IR));
  Button button_1 (.out(button_1_out));
  assign out_8 = MAR_operacao ? MAR_operador_q : 8'bz;  // Driver driver_2
  Register #(.Bits(8)) u_IR (.D({{5{1'b0}}, Op_CODE}), .C(CLK), .en(1'b1), .Q(IR_q));
  assign driver_3_out = IR ? out_8[2:0] : 3'bz;  // Driver driver_3
  Counter #(.Bits(8)) u_PC (.en(pc), .C(CLK), .clr(1'b0), .out(out_9), .ovf(PC_ovf));
  ALU8bits alu8bits_1 (.N(N), .S(driver_3_out), .CLK(CLK), .MQ(MQ_t), .neg(Negativo), .AC(AC_t), .Over(Overflow));
  assign out_8 = IR ? IR_q : 8'bz;  // Driver driver_4
  assign out_8 = pc ? out_9 : 8'bz;  // Driver driver_5
  Register #(.Bits(8)) u_AC (.D(AC_t), .C(CLK), .en(1'b1), .Q(AC));
  Register #(.Bits(8)) u_MQ (.D(MQ_t), .C(CLK), .en(1'b1), .Q(MQ));
  // also tied to GND on the sheet: PC_ovf

  // Other names for the same wires on the sheet: bus[7:0] = out_8; IR_operacao[2:0] = Op_CODE

  // Notes on the sheet:
  //   contents of Operandos (hex, n*v repeats v):
  //   1,2,3,4,5,6
  //   contents of Operações (hex, n*v repeats v):
  //   0,0,2,1,4,7
endmodule
