// Digital circuit ALU8bits.dig as structural Verilog
module ALU8bits (
  input  [7:0] N,
  input  [2:0] S,
  input  CLK,
  output [7:0] MQ,
  output neg,
  output [7:0] AC,
  output Over
);

  wire neg_t, Over_t, sMQ;
  wire [7:0] _000, _001, _010, _011, _100, _101, _110, _111, MQ0, MQ1, multiplexer_1_out, multiplexer_2_out;

  Multiplexer #(.Bits(8)) multiplexer_1 (.sel(sMQ), .in_0(MQ0), .in_1(MQ1), .out(multiplexer_1_out));
  Register #(.Bits(8)) u_MQ (.D(multiplexer_1_out), .C(CLK), .en(1'b1), .Q(MQ));
  and and_1 (sMQ, S[0], S[1], ~S[2]);  // And
  Register #(.Bits(8)) u_AC (.D(multiplexer_2_out), .C(CLK), .en(1'b1), .Q(AC));
  Multiplexer #(.Selector_Bits(3), .Bits(8)) multiplexer_2 (
    .sel(S), .in_0(_000), .in_1(_001), .in_2(_010), .in_3(_011), .in_4(_100), .in_5(_101), .in_6(_110),
    .in_7(_111), .out(multiplexer_2_out));
  and and_2 (Over, Over_t, ~S[0], ~S[1], ~S[2]);  // And
  and and_3 (neg, neg_t, S[0], ~S[1], ~S[2]);  // And
  shift_direito shift_direito_1 (.A(AC), .C_OUT(_100));
  shift_esquerdo shift_esquerdo_1 (.A(AC), .C_OUT(_101));
  nand_8bits nand_8bits_1 (.A(AC), .N(N), .AC_OUT(_110));
  xor_8bits xor_8bits_1 (.A(AC), .N(N), .AC_OUT(_111));
  full_adder_8bits full_adder_8bits_1 (.AC(AC), .N(N), .Overflow(Over_t), .S(_000));
  full_adder_not_8bit full_adder_not_8bit_1 (.AC(AC), .N(N), .Overflow(neg_t), .S(_001));
  multiplier_8 multiplier_8_1 (.A(AC), .B(N), .AC_OUT(_010), .MQ_OUT(MQ0));
  divisor_8bits divisor_8bits_1 (.A(AC), .B(N), .Q(_011), .resto(MQ1));

  // Other names for the same wires on the sheet: sAC[2:0] = S
endmodule
