// Digital circuit divisor_8bits.dig as structural Verilog
module divisor_8bits (
  input  [7:0] A,
  input  [7:0] B,
  output [7:0] Q,
  output [7:0] resto
);

  wire R1_0, R1_1, R1_2, R1_3, R1_4, R1_5, R1_6, R2_0, R2_1, R2_2, R2_3, R2_4, R2_5, R2_6, R3_0, R3_1, R3_2,
       R3_3, R3_4, R3_5, R3_6, R4_0, R4_1, R4_2, R4_3, R4_4, R4_5, R4_6, R5_0, R5_1, R5_2, R5_3, R5_4, R5_5,
       R5_6, R6_0, R6_1, R6_2, R6_3, R6_4, R6_5, R6_6, R7_0, R7_1, R7_2, R7_3, R7_4, R7_5, R7_6;
  wire [7:7] subrestore8bits_1_r, subrestore8bits_2_r, subrestore8bits_3_r, subrestore8bits_4_r,
       subrestore8bits_5_r, subrestore8bits_6_r, subrestore8bits_7_r;

  subrestore8BITS subrestore8bits_1 (
    .A({{7{1'b0}}, A[7]}), .B(B), .s(Q[7]), .C(Q[7]),
    .R({subrestore8bits_1_r[7], R1_6, R1_5, R1_4, R1_3, R1_2, R1_1, R1_0}));
  subrestore8BITS subrestore8bits_2 (
    .A({R1_6, R1_5, R1_4, R1_3, R1_2, R1_1, R1_0, A[6]}), .B(B), .s(Q[6]), .C(Q[6]),
    .R({subrestore8bits_2_r[7], R2_6, R2_5, R2_4, R2_3, R2_2, R2_1, R2_0}));
  subrestore8BITS subrestore8bits_3 (
    .A({R2_6, R2_5, R2_4, R2_3, R2_2, R2_1, R2_0, A[5]}), .B(B), .s(Q[5]), .C(Q[5]),
    .R({subrestore8bits_3_r[7], R3_6, R3_5, R3_4, R3_3, R3_2, R3_1, R3_0}));
  subrestore8BITS subrestore8bits_4 (
    .A({R3_6, R3_5, R3_4, R3_3, R3_2, R3_1, R3_0, A[4]}), .B(B), .s(Q[4]), .C(Q[4]),
    .R({subrestore8bits_4_r[7], R4_6, R4_5, R4_4, R4_3, R4_2, R4_1, R4_0}));
  subrestore8BITS subrestore8bits_5 (
    .A({R4_6, R4_5, R4_4, R4_3, R4_2, R4_1, R4_0, A[3]}), .B(B), .s(Q[3]), .C(Q[3]),
    .R({subrestore8bits_5_r[7], R5_6, R5_5, R5_4, R5_3, R5_2, R5_1, R5_0}));
  subrestore8BITS subrestore8bits_6 (
    .A({R5_6, R5_5, R5_4, R5_3, R5_2, R5_1, R5_0, A[2]}), .B(B), .s(Q[2]), .C(Q[2]),
    .R({subrestore8bits_6_r[7], R6_6, R6_5, R6_4, R6_3, R6_2, R6_1, R6_0}));
  subrestore8BITS subrestore8bits_7 (
    .A({R6_6, R6_5, R6_4, R6_3, R6_2, R6_1, R6_0, A[1]}), .B(B), .s(Q[1]), .C(Q[1]),
    .R({subrestore8bits_7_r[7], R7_6, R7_5, R7_4, R7_3, R7_2, R7_1, R7_0}));
  subrestore8BITS subrestore8bits_8 (
    .A({R7_6, R7_5, R7_4, R7_3, R7_2, R7_1, R7_0, A[0]}), .B(B), .s(Q[0]), .C(Q[0]), .R(resto));
  // also tied to GND on the sheet: {subrestore8bits_1_r[7], subrestore8bits_2_r[7], subrestore8bits_3_r[7], subrestore8bits_4_r[7], subrestore8bits_5_r[7], subrestore8bits_6_r[7], subrestore8bits_7_r[7]}

  // Other names for the same wires on the sheet: C_OUT1 = Q[7]; C_OUT2 = Q[6]; C_OUT3 = Q[5]; C_OUT4 = Q[4];
  //   C_OUT5 = Q[3]; C_OUT6 = Q[2]; C_OUT7 = Q[1]; C_OUT8 = Q[0]; R_FINAL[7:0] = resto
endmodule
