// Digital circuit full_adder_8bits.dig as structural Verilog
module full_adder_8bits (
  input  [7:0] AC,
  input  [7:0] N,
  output Overflow,
  output [7:0] S
);

  wire full_adder_1bit_1_c_out, full_adder_1bit_2_c_out, full_adder_1bit_3_c_out, full_adder_1bit_4_c_out,
       full_adder_1bit_5_c_out, full_adder_1bit_6_c_out, full_adder_1bit_7_c_out;

  full_adder_1bit full_adder_1bit_1 (.A(AC[0]), .B(N[0]), .C_in(1'b0), .S(S[0]), .C_out(full_adder_1bit_1_c_out));
  full_adder_1bit full_adder_1bit_2 (
    .A(AC[1]), .B(N[1]), .C_in(full_adder_1bit_1_c_out), .S(S[1]), .C_out(full_adder_1bit_2_c_out));
  full_adder_1bit full_adder_1bit_3 (
    .A(AC[2]), .B(N[2]), .C_in(full_adder_1bit_2_c_out), .S(S[2]), .C_out(full_adder_1bit_3_c_out));
  full_adder_1bit full_adder_1bit_4 (
    .A(AC[3]), .B(N[3]), .C_in(full_adder_1bit_3_c_out), .S(S[3]), .C_out(full_adder_1bit_4_c_out));
  full_adder_1bit full_adder_1bit_5 (
    .A(AC[4]), .B(N[4]), .C_in(full_adder_1bit_4_c_out), .S(S[4]), .C_out(full_adder_1bit_5_c_out));
  full_adder_1bit full_adder_1bit_6 (
    .A(AC[5]), .B(N[5]), .C_in(full_adder_1bit_5_c_out), .S(S[5]), .C_out(full_adder_1bit_6_c_out));
  full_adder_1bit full_adder_1bit_7 (
    .A(AC[6]), .B(N[6]), .C_in(full_adder_1bit_6_c_out), .S(S[6]), .C_out(full_adder_1bit_7_c_out));
  full_adder_1bit full_adder_1bit_8 (.A(AC[7]), .B(N[7]), .C_in(full_adder_1bit_7_c_out), .S(S[7]), .C_out(Overflow));

  // Other names for the same wires on the sheet: A1 = AC[0]; A2 = AC[1]; A3 = AC[2]; A4 = AC[3]; A5 = AC[4];
  //   A6 = AC[5]; A7 = AC[6]; A8 = AC[7]; B1 = N[0]; B2 = N[1]; B3 = N[2]; B4 = N[3]; B5 = N[4]; B6 = N[5]; B7 = N[6];
  //   B8 = N[7]; S1 = S[0]; S2 = S[1]; S3 = S[2]; S4 = S[3]; S5 = S[4]; S6 = S[5]; S7 = S[6]; S8 = S[7]
endmodule
