// Digital circuit full_adder_not_1bit.dig as structural Verilog
module full_adder_not_1bit (
  input  A,
  input  B,
  input  C_in,
  output S,
  output C_out
);

  wire and_1_out, and_2_out, not_1_out, xor_1_out;

  not not_1 (not_1_out, B);
  xor xor_1 (xor_1_out, A, not_1_out);
  xor xor_2 (S, xor_1_out, C_in);
  and and_1 (and_1_out, A, not_1_out);
  and and_2 (and_2_out, xor_1_out, C_in);
  or or_1 (C_out, and_1_out, and_2_out);
endmodule
