// Digital circuit full_adder_not_8bit.dig as structural Verilog
module full_adder_not_8bit (
  input  [7:0] AC,
  input  [7:0] N,
  output Overflow,
  output [7:0] S
);

  wire B1, B2, B3, B4, B5, B6, B7, B8, full_adder_1bit_1_c_out, full_adder_1bit_2_c_out,
       full_adder_1bit_3_c_out, full_adder_1bit_4_c_out, full_adder_1bit_5_c_out, full_adder_1bit_6_c_out,
       full_adder_1bit_7_c_out;

  assign {B8, B7, B6, B5, B4, B3, B2, B1} = ~N;  // Not not_1, 8 bits wide
  full_adder_1bit full_adder_1bit_1 (.A(AC[0]), .B(B1), .C_in(1'b1), .S(S[0]), .C_out(full_adder_1bit_1_c_out));
  full_adder_1bit full_adder_1bit_2 (
    .A(AC[1]), .B(B2), .C_in(full_adder_1bit_1_c_out), .S(S[1]), .C_out(full_adder_1bit_2_c_out));
  full_adder_1bit full_adder_1bit_3 (
    .A(AC[2]), .B(B3), .C_in(full_adder_1bit_2_c_out), .S(S[2]), .C_out(full_adder_1bit_3_c_out));
  full_adder_1bit full_adder_1bit_4 (
    .A(AC[3]), .B(B4), .C_in(full_adder_1bit_3_c_out), .S(S[3]), .C_out(full_adder_1bit_4_c_out));
  full_adder_1bit full_adder_1bit_5 (
    .A(AC[4]), .B(B5), .C_in(full_adder_1bit_4_c_out), .S(S[4]), .C_out(full_adder_1bit_5_c_out));
  full_adder_1bit full_adder_1bit_6 (
    .A(AC[5]), .B(B6), .C_in(full_adder_1bit_5_c_out), .S(S[5]), .C_out(full_adder_1bit_6_c_out));
  full_adder_1bit full_adder_1bit_7 (
    .A(AC[6]), .B(B7), .C_in(full_adder_1bit_6_c_out), .S(S[6]), .C_out(full_adder_1bit_7_c_out));
  full_adder_1bit full_adder_1bit_8 (.A(AC[7]), .B(B8), .C_in(full_adder_1bit_7_c_out), .S(S[7]), .C_out(Overflow));

  // Other names for the same wires on the sheet: A1 = AC[0]; A2 = AC[1]; A3 = AC[2]; A4 = AC[3]; A5 = AC[4];
  //   A6 = AC[5]; A7 = AC[6]; A8 = AC[7]; S1 = S[0]; S2 = S[1]; S3 = S[2]; S4 = S[3]; S5 = S[4]; S6 = S[5]; S7 = S[6];
  //   S8 = S[7]
endmodule
