// Digital circuit multiplier_8.dig as structural Verilog
module multiplier_8 (
  input  [7:0] A,
  input  [7:0] B,
  output [7:0] AC_OUT,
  output [7:0] MQ_OUT
);

  wire A0B1, A0B2, A0B3, A0B4, A0B5, A0B6, A0B7, A1B0, A1B1, A1B2, A1B3, A1B4, A1B5, A1B6, A1B7, A2B0, A2B1,
       A2B2, A2B3, A2B4, A2B5, A2B6, A2B7, A3B0, A3B1, A3B2, A3B3, A3B4, A3B5, A3B6, A3B7, A4B0, A4B1, A4B2,
       A4B3, A4B4, A4B5, A4B6, A4B7, A5B0, A5B1, A5B2, A5B3, A5B4, A5B5, A5B6, A5B7, A6B0, A6B1, A6B2, A6B3,
       A6B4, A6B5, A6B6, A6B7, A7B0, A7B1, A7B2, A7B3, A7B4, A7B5, A7B6, A7B7, Cout0, Cout1, Cout2, Cout3,
       Cout4, Cout5, Cout6, Cout7, Cout8, Cout9, Cout10, Cout11, Cout12, Cout13, Cout14, Cout15, Cout16,
       Cout17, Cout18, Cout19, Cout20, Cout21, Cout22, Cout23, Cout24, Cout25, Cout26, Cout27, Cout28,
       Cout29, Cout30, Cout31, Cout32, Cout33, Cout34, Cout35, Cout36, Cout37, Cout38, Cout39, Cout40,
       Cout41, Cout42, Cout43, Cout44, Cout45, Cout46, Cout47, Cout48, SP0, SP1, SP2, SP3, SP4, SP5, SP6,
       SP7, SP8, SP9, SP10, SP11, SP12, SP13, SP14, SP15, SP16, SP17, SP18, SP19, SP20, SP21, SP22, SP23,
       SP24, SP25, SP26, SP27, SP28, SP29, SP30, SP31, SP32, SP33, SP34, SP35;

  and and_1 (A7B7, B[7], A[7]);
  and and_2 (A7B6, B[6], A[7]);
  and and_3 (A6B7, B[7], A[6]);
  and and_4 (A7B5, B[5], A[7]);
  and and_5 (A6B6, B[6], A[6]);
  and and_6 (A5B7, B[7], A[5]);
  and and_7 (A7B4, B[4], A[7]);
  and and_8 (A6B5, B[5], A[6]);
  and and_9 (A5B6, B[6], A[5]);
  and and_10 (A4B7, B[7], A[4]);
  and and_11 (A7B3, B[3], A[7]);
  and and_12 (A6B4, B[4], A[6]);
  and and_13 (A5B5, B[5], A[5]);
  and and_14 (A4B6, B[6], A[4]);
  and and_15 (A3B7, B[7], A[3]);
  and and_16 (A7B2, B[2], A[7]);
  and and_17 (A6B3, B[3], A[6]);
  and and_18 (A5B4, B[4], A[5]);
  and and_19 (A4B5, B[5], A[4]);
  and and_20 (A3B6, B[6], A[3]);
  and and_21 (A2B7, B[7], A[2]);
  and and_22 (A7B1, B[1], A[7]);
  and and_23 (A6B2, B[2], A[6]);
  and and_24 (A5B3, B[3], A[5]);
  and and_25 (A4B4, B[4], A[4]);
  and and_26 (A3B5, B[5], A[3]);
  and and_27 (A2B6, B[6], A[2]);
  and and_28 (A1B7, B[7], A[1]);
  and and_29 (A7B0, B[0], A[7]);
  and and_30 (A6B1, B[1], A[6]);
  and and_31 (A5B2, B[2], A[5]);
  and and_32 (A4B3, B[3], A[4]);
  and and_33 (A3B4, B[4], A[3]);
  and and_34 (A2B5, B[5], A[2]);
  and and_35 (A1B6, B[6], A[1]);
  and and_36 (A0B7, B[7], A[0]);
  and and_37 (A6B0, B[0], A[6]);
  and and_38 (A5B1, B[1], A[5]);
  and and_39 (A4B2, B[2], A[4]);
  and and_40 (A3B3, B[3], A[3]);
  and and_41 (A2B4, B[4], A[2]);
  and and_42 (A1B5, B[5], A[1]);
  and and_43 (A0B6, B[6], A[0]);
  and and_44 (A5B0, B[0], A[5]);
  and and_45 (A4B1, B[1], A[4]);
  and and_46 (A3B2, B[2], A[3]);
  and and_47 (A2B3, B[3], A[2]);
  and and_48 (A1B4, B[4], A[1]);
  and and_49 (A0B5, B[5], A[0]);
  and and_50 (A4B0, B[0], A[4]);
  and and_51 (A3B1, B[1], A[3]);
  and and_52 (A2B2, B[2], A[2]);
  and and_53 (A1B3, B[3], A[1]);
  and and_54 (A0B4, B[4], A[0]);
  and and_55 (A3B0, B[0], A[3]);
  and and_56 (A2B1, B[1], A[2]);
  and and_57 (A1B2, B[2], A[1]);
  and and_58 (A0B3, B[3], A[0]);
  and and_59 (A2B0, B[0], A[2]);
  and and_60 (A1B1, B[1], A[1]);
  and and_61 (A0B2, B[2], A[0]);
  and and_62 (A1B0, B[0], A[1]);
  and and_63 (A0B1, B[1], A[0]);
  and and_64 (AC_OUT[0], B[0], A[1]);
  full_adder_1bit A1B0__plus__A0B1 (.A(A1B0), .B(A0B1), .C_in(1'b0), .S(AC_OUT[1]), .C_out(Cout0));
  full_adder_1bit A2B0__plus__A1B1 (.A(A2B0), .B(A1B1), .C_in(Cout0), .S(SP0), .C_out(Cout1));
  full_adder_1bit A3B0__plus__A2B1 (.A(A3B0), .B(A2B1), .C_in(Cout1), .S(SP1), .C_out(Cout3));
  full_adder_1bit A4B0__plus__A3B1 (.A(A4B0), .B(A3B1), .C_in(Cout3), .S(SP3), .C_out(Cout6));
  full_adder_1bit A5B0__plus__A4B1 (.A(A5B0), .B(A4B1), .C_in(Cout6), .S(SP6), .C_out(Cout10));
  full_adder_1bit A6B0__plus__A5B1 (.A(A6B0), .B(A5B1), .C_in(Cout10), .S(SP10), .C_out(Cout15));
  full_adder_1bit A7B0__plus__A6B1 (.A(A7B0), .B(A6B1), .C_in(Cout15), .S(SP15), .C_out(Cout21));
  full_adder_1bit A7B1__plus__A6B2 (.A(A7B1), .B(A6B2), .C_in(Cout21), .S(SP21), .C_out(Cout28));
  full_adder_1bit A7B2__plus__A6B3 (.A(A7B2), .B(A6B3), .C_in(Cout28), .S(SP26), .C_out(Cout34));
  full_adder_1bit A7B3__plus__A6B4 (.A(A7B3), .B(A6B4), .C_in(Cout34), .S(SP30), .C_out(Cout39));
  full_adder_1bit A7B4__plus__A6B5 (.A(A7B4), .B(A6B5), .C_in(Cout39), .S(SP33), .C_out(Cout43));
  full_adder_1bit A7B5__plus__A6B6 (.A(A7B5), .B(A6B6), .C_in(Cout43), .S(SP35), .C_out(Cout46));
  full_adder_1bit full_adder_1bit_1 (.A(A7B6), .B(A6B7), .C_in(Cout46), .S(MQ_OUT[5]), .C_out(Cout48));
  full_adder_1bit full_adder_1bit_2 (.A(A7B7), .B(Cout48), .C_in(1'b0), .S(MQ_OUT[6]), .C_out(MQ_OUT[7]));
  full_adder_1bit SP0__plus__A0B2 (.A(A0B2), .B(SP0), .C_in(1'b0), .S(AC_OUT[2]), .C_out(Cout2));
  full_adder_1bit A1B2__plus__SP1 (.A(A1B2), .B(SP1), .C_in(Cout2), .S(SP2), .C_out(Cout4));
  full_adder_1bit A2B2__plus__SP3 (.A(A2B2), .B(SP3), .C_in(Cout4), .S(SP4), .C_out(Cout7));
  full_adder_1bit A3B2__plus__SP6 (.A(A3B2), .B(SP6), .C_in(Cout7), .S(SP7), .C_out(Cout11));
  full_adder_1bit A4B2__plus__SP10 (.A(A4B2), .B(SP10), .C_in(Cout11), .S(SP11), .C_out(Cout16));
  full_adder_1bit A5B2__plus__SP15 (.A(A5B2), .B(SP15), .C_in(Cout16), .S(SP16), .C_out(Cout22));
  full_adder_1bit A5B3__plus__SP21 (.A(A5B3), .B(SP21), .C_in(Cout22), .S(SP22), .C_out(Cout29));
  full_adder_1bit A5B4__plus__SP26 (.A(A5B4), .B(SP26), .C_in(Cout29), .S(SP27), .C_out(Cout35));
  full_adder_1bit A5B5__plus__SP32 (.A(A5B5), .B(SP30), .C_in(Cout35), .S(SP31), .C_out(Cout40));
  full_adder_1bit A5B6__plus__SP35 (.A(A5B6), .B(SP33), .C_in(Cout40), .S(SP34), .C_out(Cout44));
  full_adder_1bit A5B7__plus__SP37 (.A(A5B7), .B(SP35), .C_in(Cout44), .S(MQ_OUT[4]), .C_out(Cout47));
  full_adder_1bit A0B3__plus__SP2 (.A(A0B3), .B(SP2), .C_in(1'b0), .S(AC_OUT[3]), .C_out(Cout5));
  full_adder_1bit A1B3__plus__SP4 (.A(A1B3), .B(SP4), .C_in(Cout5), .S(SP5), .C_out(Cout8));
  full_adder_1bit A2B3__plus__SP7 (.A(A2B3), .B(SP7), .C_in(Cout8), .S(SP8), .C_out(Cout12));
  full_adder_1bit A3B3__plus__SP11 (.A(A3B3), .B(SP11), .C_in(Cout12), .S(SP12), .C_out(Cout17));
  full_adder_1bit A4B3__plus__SP16 (.A(A4B3), .B(SP16), .C_in(Cout17), .S(SP17), .C_out(Cout23));
  full_adder_1bit A4B4__plus__SP22 (.A(A4B4), .B(SP22), .C_in(Cout23), .S(SP23), .C_out(Cout30));
  full_adder_1bit A4B5__plus__SP27 (.A(A4B5), .B(SP27), .C_in(Cout30), .S(SP28), .C_out(Cout36));
  full_adder_1bit A4B6__plus__SP33 (.A(A4B6), .B(SP31), .C_in(Cout36), .S(SP32), .C_out(Cout41));
  full_adder_1bit A4B7__plus__SP36 (.A(A4B7), .B(SP34), .C_in(Cout41), .S(MQ_OUT[3]), .C_out(Cout45));
  full_adder_1bit A0B4__plus__SP5 (.A(A0B4), .B(SP5), .C_in(1'b0), .S(AC_OUT[4]), .C_out(Cout9));
  full_adder_1bit A1B4__plus__SP8 (.A(A1B4), .B(SP8), .C_in(Cout9), .S(SP9), .C_out(Cout13));
  full_adder_1bit A2B4__plus__SP12 (.A(A2B4), .B(SP12), .C_in(Cout13), .S(SP13), .C_out(Cout18));
  full_adder_1bit A3B4__plus__SP17 (.A(A3B4), .B(SP17), .C_in(Cout18), .S(SP18), .C_out(Cout24));
  full_adder_1bit A3B5__plus__SP23 (.A(A3B5), .B(SP23), .C_in(Cout24), .S(SP24), .C_out(Cout31));
  full_adder_1bit A3B6__plus__SP28 (.A(A3B6), .B(SP28), .C_in(Cout31), .S(SP29), .C_out(Cout37));
  full_adder_1bit A3B7__plus__SP34 (.A(A3B7), .B(SP32), .C_in(Cout37), .S(MQ_OUT[2]), .C_out(Cout42));
  full_adder_1bit A0B5__plus__SP9 (.A(A0B5), .B(SP9), .C_in(1'b0), .S(AC_OUT[5]), .C_out(Cout14));
  full_adder_1bit A1B5__plus__SP13 (.A(A1B5), .B(SP13), .C_in(Cout14), .S(SP14), .C_out(Cout19));
  full_adder_1bit A2B5__plus__SP18 (.A(A2B5), .B(SP18), .C_in(Cout19), .S(SP19), .C_out(Cout25));
  full_adder_1bit A2B6__plus__SP24 (.A(A2B6), .B(SP24), .C_in(Cout25), .S(SP25), .C_out(Cout32));
  full_adder_1bit A2B7__plus__SP29 (.A(A2B7), .B(SP29), .C_in(Cout32), .S(MQ_OUT[1]), .C_out(Cout38));
  full_adder_1bit A0B6__plus__AP14 (.A(A0B6), .B(SP14), .C_in(1'b0), .S(AC_OUT[6]), .C_out(Cout20));
  full_adder_1bit A1B6__plus__SP19 (.A(A1B6), .B(SP19), .C_in(Cout20), .S(SP20), .C_out(Cout26));
  full_adder_1bit A1B7__plus__SP25 (.A(A1B7), .B(SP25), .C_in(Cout26), .S(MQ_OUT[0]), .C_out(Cout33));
  full_adder_1bit A0B7__plus__SP20 (.A(A0B7), .B(SP20), .C_in(1'b0), .S(AC_OUT[7]), .C_out(Cout27));

  // Other names for the same wires on the sheet: AC0 = AC_OUT[0]; AC1 = AC_OUT[1]; AC2 = AC_OUT[2]; AC3 = AC_OUT[3];
  //   AC4 = AC_OUT[4]; AC5 = AC_OUT[5]; AC6 = AC_OUT[6]; AC7 = AC_OUT[7]; MQ0 = MQ_OUT[0]; MQ1 = MQ_OUT[1];
  //   MQ2 = MQ_OUT[2]; MQ3 = MQ_OUT[3]; MQ4 = MQ_OUT[4]; MQ5 = MQ_OUT[5]; MQ6 = MQ_OUT[6]; MQ7 = MQ_OUT[7]
endmodule
