// Digital circuit nand_8bits.dig as structural Verilog
module nand_8bits (
  input  [7:0] A,
  input  [7:0] N,
  output [7:0] AC_OUT
);

  assign AC_OUT = ~(A & N);  // NAnd nand_1, 8 bits wide
endmodule
