// Digital circuit subrestore1BIT.dig as structural Verilog
module subrestore1BIT (
  input  C_IN,
  input  A,
  input  B,
  input  S,
  output C_OUT,
  output R
);

  wire tBnot, tSub;

  not not_1 (tBnot, B);
  selector_1bit selector_1bit_1 (.C_IN(A), .A(tBnot), .B(C_IN), .S(tSub), .C_OUT(C_OUT));
  Multiplexer multiplexer_1 (.sel(S), .in_0(A), .in_1(tSub), .out(R));

  // Other names for the same wires on the sheet: tA = A; tCin = C_IN; tCout = C_OUT
endmodule
