// Digital circuit subrestore8BITS.dig as structural Verilog
module subrestore8BITS (
  input  [7:0] A,
  input  [7:0] B,
  input  s,
  output C,
  output [7:0] R
);

  wire subrestore1bit_1_c_out, subrestore1bit_2_c_out, subrestore1bit_3_c_out, subrestore1bit_4_c_out,
       subrestore1bit_5_c_out, subrestore1bit_6_c_out, subrestore1bit_7_c_out;

  subrestore1BIT subrestore1bit_1 (.C_IN(1'b1), .A(A[0]), .B(B[0]), .S(s), .C_OUT(subrestore1bit_1_c_out), .R(R[0]));
  subrestore1BIT subrestore1bit_2 (
    .C_IN(subrestore1bit_1_c_out), .A(A[1]), .B(B[1]), .S(s), .C_OUT(subrestore1bit_2_c_out), .R(R[1]));
  subrestore1BIT subrestore1bit_3 (
    .C_IN(subrestore1bit_2_c_out), .A(A[2]), .B(B[2]), .S(s), .C_OUT(subrestore1bit_3_c_out), .R(R[2]));
  subrestore1BIT subrestore1bit_4 (
    .C_IN(subrestore1bit_3_c_out), .A(A[3]), .B(B[3]), .S(s), .C_OUT(subrestore1bit_4_c_out), .R(R[3]));
  subrestore1BIT subrestore1bit_5 (
    .C_IN(subrestore1bit_4_c_out), .A(A[4]), .B(B[4]), .S(s), .C_OUT(subrestore1bit_5_c_out), .R(R[4]));
  subrestore1BIT subrestore1bit_6 (
    .C_IN(subrestore1bit_5_c_out), .A(A[5]), .B(B[5]), .S(s), .C_OUT(subrestore1bit_6_c_out), .R(R[5]));
  subrestore1BIT subrestore1bit_7 (
    .C_IN(subrestore1bit_6_c_out), .A(A[6]), .B(B[6]), .S(s), .C_OUT(subrestore1bit_7_c_out), .R(R[6]));
  subrestore1BIT subrestore1bit_8 (.C_IN(subrestore1bit_7_c_out), .A(A[7]), .B(B[7]), .S(s), .C_OUT(C), .R(R[7]));
endmodule
