// Digital circuit ringcounter_5bits.dig as structural Verilog
module ringcounter_5bits (
  input  clk,
  input  btn,
  output Q0,
  output Q1,
  output Q2,
  output Q3,
  output Q4
);

  D_FF_AS d_ff_as_1 (.Set(btn), .D(Q4), .C(clk), .Clr(1'b0), .Q(Q0));  // open: nQ
  LED led_1 (.in(Q0));
  D_FF_AS d_ff_as_2 (.Set(1'b0), .D(Q0), .C(clk), .Clr(1'b0), .Q(Q1));  // open: nQ
  LED led_2 (.in(Q1));
  D_FF_AS d_ff_as_3 (.Set(1'b0), .D(Q1), .C(clk), .Clr(1'b0), .Q(Q2));  // open: nQ
  LED led_3 (.in(Q2));
  D_FF_AS d_ff_as_4 (.Set(1'b0), .D(Q2), .C(clk), .Clr(1'b0), .Q(Q3));  // open: nQ
  LED led_4 (.in(Q3));
  D_FF_AS d_ff_as_5 (.Set(1'b0), .D(Q3), .C(clk), .Clr(1'b0), .Q(Q4));  // open: nQ
  LED led_5 (.in(Q4));
endmodule
